# Fritzing sketch PC2_DistanceCompanion_circuit (saved by Fritzing 0.9.4)

parts:
  ESP8266 = NodeMCU V3.0
  Nokia_5110_LCD_Module = Nokia 5110 LCD
  S1 = Pushbutton [package="[THT]"]

nets:
  N1: ESP8266.D0, ESP8266.RST, S1.Pin_1, S1.Pin_2
  N2: ESP8266.D1, Nokia_5110_LCD_Module.CE
  N3: ESP8266.D2, Nokia_5110_LCD_Module.D/C
  N4: ESP8266.D3, Nokia_5110_LCD_Module.Din
  N5: ESP8266.D4, Nokia_5110_LCD_Module.CLK
  3V3: ESP8266.3V3, Nokia_5110_LCD_Module.VCC
  GND: ESP8266.GND, Nokia_5110_LCD_Module.GND, S1.Pin_3, S1.Pin_4
  N6: ESP8266.D5, Nokia_5110_LCD_Module.BL
  N7: ESP8266.D6, Nokia_5110_LCD_Module.RST

custom parts:
  NodeMCU V3.0: NodeMcu V3 Lua WIFI Development Board
  Nokia 5110 LCD: Nokia 5110 Graphic 84*48 LCD module <Blue Version>
